// Logisim project Code_Grey.circ as structural Verilog: 3 circuits, main circuit main
module main (
  input  [3:0] in_1,
  input  [3:0] in_2,
  output [3:0] out_3,
  output out_4,
  output [3:0] out_5
);

  wire adder_1_cout, and_1_out, and_2_out;
  wire [3:0] adder_1_out, gray_to_bin_1_b0, gray_to_bin_2_b0;

  Gray_to_Bin gray_to_bin_1 (
    .G3(in_1[3]), .G2(in_1[2]), .G1(in_1[1]), .G0(in_1[0]), .B3(gray_to_bin_1_b0[3]),
    .B2(gray_to_bin_1_b0[2]), .B1(gray_to_bin_1_b0[1]), .B0(gray_to_bin_1_b0[0]));
  Gray_to_Bin gray_to_bin_2 (
    .G3(in_2[3]), .G2(in_2[2]), .G1(in_2[1]), .G0(in_2[0]), .B3(gray_to_bin_2_b0[3]),
    .B2(gray_to_bin_2_b0[2]), .B1(gray_to_bin_2_b0[1]), .B0(gray_to_bin_2_b0[0]));
  Adder #(.width(4)) adder_1 (
    .a(gray_to_bin_1_b0), .b(gray_to_bin_2_b0), .out(adder_1_out), .cin(1'b1), .cout(adder_1_cout));
  Adder #(.width(4)) adder_2 (.a(adder_1_out), .b({1'b0, {2{out_4}}, 1'b0}), .out(out_5));  // open: cin, cout
  and and_1 (and_1_out, adder_1_out[2], adder_1_out[3]);
  and and_2 (and_2_out, adder_1_out[1], adder_1_out[3]);
  or or_1 (out_4, and_1_out, and_2_out, adder_1_cout);
  Bin_to_Gray bin_to_gray_1 (
    .B3(out_5[3]), .B2(out_5[2]), .B1(out_5[1]), .B0(out_5[0]), .G3(out_3[3]), .G2(out_3[2]), .G1(out_3[1]),
    .G0(out_3[0]));
endmodule

module Gray_to_Bin (
  input  G3,
  input  G2,
  input  G1,
  input  G0,
  output B3,
  output B2,
  output B1,
  output B0
);

  wire and_2_out, and_3_out, and_4_out, and_5_out, and_6_out, and_7_out, and_8_out, not_1_out, not_2_out,
       not_3_out, not_4_out;

  not not_1 (not_1_out, G3);
  not not_2 (not_2_out, G2);
  not not_3 (not_3_out, G1);
  not not_4 (not_4_out, G0);
  and and_1 (B2, not_1_out, G2);
  and and_2 (and_2_out, not_2_out, G1);
  and and_3 (and_3_out, not_1_out, G2, not_3_out);
  and and_4 (and_4_out, not_2_out, not_3_out, G0);
  and and_5 (and_5_out, not_2_out, G1, not_4_out);
  and and_6 (and_6_out, not_1_out, G2, not_3_out, not_4_out);
  and and_7 (and_7_out, G2, G1, G0);
  and and_8 (and_8_out, G3, G0);
  or or_1 (B1, and_2_out, and_3_out);
  or or_2 (B0, and_4_out, and_5_out, and_6_out, and_7_out, and_8_out);

  assign B3 = G3;
endmodule

module Bin_to_Gray (
  input  B3,
  input  B2,
  input  B1,
  input  B0,
  output G3,
  output G2,
  output G1,
  output G0
);

  wire and_1_out, and_2_out, and_3_out, and_4_out, not_1_out, not_2_out, not_3_out;

  not not_1 (not_1_out, B2);
  not not_2 (not_2_out, B1);
  not not_3 (not_3_out, B0);
  or or_1 (G2, B2, B3);
  and and_1 (and_1_out, not_1_out, B1);
  and and_2 (and_2_out, B2, not_2_out);
  and and_3 (and_3_out, not_2_out, B0);
  and and_4 (and_4_out, B1, not_3_out);
  or or_2 (G1, and_1_out, and_2_out);
  or or_3 (G0, and_3_out, and_4_out);

  assign G3 = B3;
endmodule
